# Fritzing sketch DualMotorDriver (saved by Fritzing 0.9.3b)
circuit board: 8.46667cm x 5.64444cm
breadboards: 1

parts:
  driver = Motor Driver 1A Dual TB6612FNG
  M3 = DC Motor
  M4 = DC Motor
  Raspberry_Pi_Model_B1 = Raspberry Pi 3 [part_number=RPI-3-V1.2]

nets:
  GND: driver.GND, Raspberry_Pi_Model_B1.GND
  N1: driver.B01, M4.pin_1
  N2: driver.B02, M4.pin_2
  N3: driver.A02, M3.pin_1
  N4: driver.A01, M3.pin_2
  N5: driver.VCC, Raspberry_Pi_Model_B1.GPIO21
  N6: driver.VM, Raspberry_Pi_Model_B1.5V
  N7: driver.PWMA, Raspberry_Pi_Model_B1.GPIO13
  N8: driver.AIN2, Raspberry_Pi_Model_B1.GPIO6
  N9: driver.AIN1, Raspberry_Pi_Model_B1.GPIO10
  N10: driver.STBY, Raspberry_Pi_Model_B1.GPIO9
  N11: driver.BIN1, Raspberry_Pi_Model_B1.GPIO11
  N12: driver.BIN2, Raspberry_Pi_Model_B1.GPIO5
  N13: driver.PWMB, Raspberry_Pi_Model_B1.GPIO18

notes:
  Gurwarris Sohi
  n01266020
