# Fritzing sketch GurwarrisSohi_SmartTennisBallMachine V2 (saved by Fritzing 0.9.3b)
circuit board: 8.41966cm x 6.76868cm
breadboards: 1

parts:
  Part1 = Motor Driver 1A Dual TB6612FNG
  J1 = Basic Servo
  M1 = DC Motor
  M2 = DC Motor
  VCC1 = Battery block 9V
  R1 = Resistor [tolerance=±5% resistance=2.2k package="2010 [SMD]"]
  D1 = Rectifier Diode [part_number=1N4001 package="Melf DO-213 AB [SMD]"]
  L1 = Solenoid
  Raspberry_Pi_1 = Raspberry Pi 3 [part_number=RPI-3-V1.2]
  MOSFET-_30N06L1 = Basic FET P-Channel [package="D2Pak [SMD]"]

nets:
  GND: Part1.GND, J1.gnd, VCC1.-, Raspberry_Pi_1.GND
  N1: Part1.B01, M1.pin_1
  N2: Part1.B02, M1.pin_2
  N3: Part1.A02, M2.pin_1
  N4: Part1.A01, M2.pin_2
  VCC: Part1.VCC, J1.vcc, Raspberry_Pi_1.5V
  N5: Part1.VM, VCC1.+, D1.cathode, L1.pin2
  N6: Part1.PWMA, Raspberry_Pi_1.GPIO21
  N7: Part1.AIN2, Raspberry_Pi_1.GPIO16
  N8: Part1.AIN1, Raspberry_Pi_1.GPIO12
  N9: Part1.STBY, Raspberry_Pi_1.GPIO26
  N10: Part1.BIN1, Raspberry_Pi_1.GPIO6
  N11: Part1.BIN2, Raspberry_Pi_1.GPIO13
  N12: Part1.PWMB, Raspberry_Pi_1.GPIO20
  N13: J1.pulse, Raspberry_Pi_1.GPIO18
  N14: R1.Pin_0, Raspberry_Pi_1.GPIO4
  N15: R1.Pin_1, MOSFET-_30N06L1.Gate
  N16: D1.anode, MOSFET-_30N06L1.source
  N17: L1.pin1, MOSFET-_30N06L1.drain

notes:
  Gurwarris Sohi Smart PingPong
