# Fritzing sketch Seloenoid Fritz (saved by Fritzing 0.9.3b)
circuit board: 4.14461cm x 2.98318cm
breadboards: 1

parts:
  JP1 = Header 3 [package=screwterminal-3.5mm-3_lock.007s]
  VCC1 = Battery
  J1 = Generic female header - 2 pins [form="♀ (female)" package=THT]  # not connected
  J2 = Generic female header - 2 pins [form="♀ (female)" package=THT]
  J3 = Generic female header - 2 pins [form="♀ (female)" package=THT]  # not connected
  J4 = Generic female header - 2 pins [form="♀ (female)" package=THT]

nets:
  N1: JP1.1, J4.pin1
  N2: JP1.2, VCC1.-, J2.pin2
  N3: JP1.3, VCC1.+

notes:
  Sahil

custom parts:
  Generic female header - 2 pins: Generic female header
