# Fritzing sketch Servo Fritz (saved by Fritzing 0.9.3b)
circuit board: 6.35522cm x 5.83728cm
breadboards: 1

parts:
  J1 = Basic Servo
  Q1 = NPN-Transistor [package="TO92 [THT]"]
  LED3 = LED - 3mm [color="Red (633nm)" package="3 mm [THT]"]
  R1 = Resistor [tolerance=±5% resistance=220 package=THT]
  R2 = Resistor [tolerance=±5% resistance=2.2k package=THT]
  Servo_Motor_Project = Raspberry Pi 3 [part_number=RPI-3-V1.2]

nets:
  GND: J1.gnd, Q1.E, Servo_Motor_Project.GND
  VCC: J1.vcc, R1.Pin_0, Servo_Motor_Project.5V
  N1: J1.pulse, Servo_Motor_Project.GIPO18
  N2: Q1.B, R2.Pin_1
  N3: Q1.C, LED3.cathode
  N4: LED3.anode, R1.Pin_1
  N5: R2.Pin_0, Servo_Motor_Project.GIPO21

notes:
  EMITTER
  COLLECTOR
  BASE
  GND
  VCC
  PULSE
  Nicolas Cristiano
